// Logisim project Base.circ as structural Verilog: 28 circuits, main circuit main
module main (
);

  wire clock_1_out, cpu_1_halt, frontpanelcontroller_1_cpuclk, frontpanelcontroller_1_runhalt, Reset_out,
       RunStop_out, Step_out;
  wire [3:0] cpu_1_aluflags, cpu_1_flags;
  wire [15:0] cpu_1_alua, cpu_1_alub, cpu_1_aluresult, cpu_1_dmaddress, cpu_1_dmdata, cpu_1_imaddress,
       cpu_1_imdata, cpu_1_writeback, IM_data;

  Clock clock_1 (.out(clock_1_out));
  ROM #(.addrWidth(16), .dataWidth(16)) IM (.addr(cpu_1_imaddress), .data(IM_data));
  FrontPanelController frontpanelcontroller_1 (
    .Clk(clock_1_out), .Run(RunStop_out), .Step(Step_out), .Reset(Reset_out), .Halt(cpu_1_halt),
    .CpuClk(frontpanelcontroller_1_cpuclk), .RunHalt(frontpanelcontroller_1_runhalt));
  CPU cpu_1 (
    .Reset(Reset_out), .CLK(frontpanelcontroller_1_cpuclk), .IMDataIn(IM_data), .Halt(cpu_1_halt),
    .IMAddress(cpu_1_imaddress), .IMData(cpu_1_imdata), .DMAddress(cpu_1_dmaddress), .DMData(cpu_1_dmdata),
    .WriteBack(cpu_1_writeback), .Flags(cpu_1_flags), .AluA(cpu_1_alua), .AluB(cpu_1_alub),
    .ALUResult(cpu_1_aluresult), .ALUFlags(cpu_1_aluflags));
  LED led_1 (.in(cpu_1_flags[3]));
  LED led_2 (.in(cpu_1_flags[2]));
  LED led_3 (.in(cpu_1_flags[1]));
  LED led_4 (.in(cpu_1_flags[0]));
  Hex_Digit_Display hex_digit_display_1 (.value(cpu_1_alua[15:12]));  // open: dp
  LED led_5 (.in(cpu_1_halt));
  Hex_Digit_Display hex_digit_display_2 (.value(cpu_1_imaddress[15:12]));  // open: dp
  Hex_Digit_Display hex_digit_display_3 (.value(cpu_1_imaddress[11:8]));  // open: dp
  Hex_Digit_Display hex_digit_display_4 (.value(cpu_1_imdata[15:12]));  // open: dp
  Hex_Digit_Display hex_digit_display_5 (.value(cpu_1_imdata[11:8]));  // open: dp
  Hex_Digit_Display hex_digit_display_6 (.value(cpu_1_alua[11:8]));  // open: dp
  Hex_Digit_Display hex_digit_display_7 (.value(cpu_1_alua[7:4]));  // open: dp
  LED N (.in(cpu_1_aluflags[3]));
  LED Z (.in(cpu_1_aluflags[2]));
  LED C (.in(cpu_1_aluflags[1]));
  LED led_6 (.in(frontpanelcontroller_1_runhalt));
  Button RunStop (.out(RunStop_out));
  Hex_Digit_Display hex_digit_display_8 (.value(cpu_1_imaddress[7:4]));  // open: dp
  Hex_Digit_Display hex_digit_display_9 (.value(cpu_1_imaddress[3:0]));  // open: dp
  Hex_Digit_Display hex_digit_display_10 (.value(cpu_1_imdata[7:4]));  // open: dp
  // Hex_Digit_Display hex_digit_display_11: pin names not known; wires that end beside it: cpu_1_imdata[3:0]
  Hex_Digit_Display hex_digit_display_12 (.value(cpu_1_alua[3:0]));  // open: dp
  LED V (.in(cpu_1_aluflags[0]));
  Button Step (.out(Step_out));
  Hex_Digit_Display hex_digit_display_13 (.value(cpu_1_dmaddress[15:12]));  // open: dp
  Hex_Digit_Display hex_digit_display_14 (.value(cpu_1_dmdata[15:12]));  // open: dp
  Hex_Digit_Display hex_digit_display_15 (.value(cpu_1_writeback[15:12]));  // open: dp
  Hex_Digit_Display hex_digit_display_16 (.value(cpu_1_alub[15:12]));  // open: dp
  Hex_Digit_Display hex_digit_display_17 (.value(cpu_1_aluresult[15:12]));  // open: dp
  Button Reset (.out(Reset_out));
  Hex_Digit_Display hex_digit_display_18 (.value(cpu_1_dmaddress[11:8]));  // open: dp
  Hex_Digit_Display hex_digit_display_19 (.value(cpu_1_dmaddress[7:4]));  // open: dp
  Hex_Digit_Display hex_digit_display_20 (.value(cpu_1_dmdata[11:8]));  // open: dp
  Hex_Digit_Display hex_digit_display_21 (.value(cpu_1_dmdata[7:4]));  // open: dp
  Hex_Digit_Display hex_digit_display_22 (.value(cpu_1_writeback[11:8]));  // open: dp
  Hex_Digit_Display hex_digit_display_23 (.value(cpu_1_writeback[7:4]));  // open: dp
  Hex_Digit_Display hex_digit_display_24 (.value(cpu_1_alub[11:8]));  // open: dp
  Hex_Digit_Display hex_digit_display_25 (.value(cpu_1_alub[7:4]));  // open: dp
  Hex_Digit_Display hex_digit_display_26 (.value(cpu_1_aluresult[11:8]));  // open: dp
  Hex_Digit_Display hex_digit_display_27 (.value(cpu_1_aluresult[7:4]));  // open: dp
  Hex_Digit_Display hex_digit_display_28 (.value(cpu_1_dmaddress[3:0]));  // open: dp
  Hex_Digit_Display hex_digit_display_29 (.value(cpu_1_dmdata[3:0]));  // open: dp
  Hex_Digit_Display hex_digit_display_30 (.value(cpu_1_writeback[3:0]));  // open: dp
  Hex_Digit_Display hex_digit_display_31 (.value(cpu_1_alub[3:0]));  // open: dp
  Hex_Digit_Display hex_digit_display_32 (.value(cpu_1_aluresult[3:0]));  // open: dp

  // Notes on the sheet:
  //   contents of IM (hex, n*v repeats v):
  //   8080 9000 1040 a000 b001 2209 7003 9000 1889 600 9001 2209 7005 9000 1889 9001 184a 600 8080 9000
  //   1040 a000 b001 188a 204b 188b a001 b001 c000 2203 10ac 22b3 11b4 214e 2093 188c 2203 6001 4ff7 600
  //   N  Z  C  V
  //   Latched Flags
  //   HALT
  //   Instruction Memory
  //   mARMi
  //   ALU A Input
  //   ALU Flags
  //   Data Memory
  //   WriteBack
  //   ALU B Input
  //   ALU Result
endmodule

module CPU (
  input  Reset,
  input  CLK,
  input  [15:0] IMDataIn,
  output Halt,
  output [15:0] IMAddress,
  output [15:0] IMData,
  output [15:0] DMAddress,
  output [15:0] DMData,
  output [15:0] WriteBack,
  output [3:0] Flags,
  output [15:0] AluA,
  output [15:0] AluB,
  output [15:0] ALUResult,
  output [3:0] ALUFlags
);

  wire CLKin, isLoad, isLoadOrStore, isR7, isStore, isWriteEnableR7, JMP, multiplexer_4_out,
       multiplexer_6_out, nonaluops_1_isflag, or_1_out, WE3, WE3Out;
  wire [2:0] A1, A1Out, A2, A2Out, A3, A3Out, LoadStoreRd, LoadStoreRm, LoadStoreRn;
  wire [3:0] AddOp, alu_1_flagsnzcv, controller_1_opcode, OpCode;
  wire [11:0] extractimm_1_out_2;
  wire [15:0] ImmOut, movData, multiplexer_5_out, nonaluops_1_flagsout, PCOut, PCPlus1, R7Write, RD1, RD2,
       Store, WD3, WD3Out;

  ExtractImm extractimm_1 (.in_1(IMDataIn), .out_2(extractimm_1_out_2));
  isNopHalt isnophalt_1 (.Instruction(IMDataIn), .isHalt(Halt));  // open: isNOP
  nonALUOps nonaluops_1 (
    .Instruction(IMDataIn), .Flags(Flags), .flagsOut(nonaluops_1_flagsout), .isFlag(nonaluops_1_isflag));
  Multiplexer #(.width(16)) multiplexer_1 (
    .in0(RD1), .in1(nonaluops_1_flagsout), .out(movData), .sel(nonaluops_1_isflag));
  RegisterFileControl registerfilecontrol_1 (
    .isLoadOrStore(isLoadOrStore), .WE3(WE3), .A1(A1), .LoadStoreRm(LoadStoreRm), .A2(A2),
    .LoadStoreRn(LoadStoreRn), .A3(A3), .LoadStoreRd(LoadStoreRd), .WD3(WD3), .DMData(DMData),
    .isLoad(isLoad), .WE3Out(WE3Out), .A1Out(A1Out), .A2Out(A2Out), .A3Out(A3Out), .WD3Out(WD3Out));  // open: in_12
  Controller controller_1 (
    .Instr(IMDataIn), .ALUResult(ALUResult), .MovData(movData), .Imm(extractimm_1_out_2), .A3(A3), .A2(A2),
    .A1(A1), .WD3(WD3), .WE3(WE3), .OpCode(controller_1_opcode));
  conditionalCircuit conditionalcircuit_1 (
    .PCPlus1(PCPlus1), .Instruction(IMDataIn), .LatchedFlags(Flags), .PCOut(PCOut), .ImmOut(ImmOut),
    .JMP(JMP), .Opcode(AddOp));
  LoadStore loadstore_1 (
    .Instruction(IMDataIn), .Rd(LoadStoreRd), .Rm(LoadStoreRm), .Rn(LoadStoreRn), .isLoad(isLoad),
    .isLoadOrStore(isLoadOrStore), .isStore(isStore));
  and and_1 (CLKin, ~Halt, CLK);  // AND_Gate
  Multiplexer #(.width(4)) multiplexer_2 (.in0(controller_1_opcode), .in1(AddOp), .out(OpCode), .sel(or_1_out));
  or or_1 (or_1_out, JMP, isLoadOrStore);
  Multiplexer #(.width(16)) multiplexer_3 (.in0({16{1'b0}}), .in1(WD3Out), .out(WriteBack), .sel(WE3Out));
  Multiplexer multiplexer_4 (.in0(1'b0), .in1(1'b1), .out(multiplexer_4_out), .sel(isStore));
  Multiplexer #(.width(16)) multiplexer_5 (
    .in0(ALUResult), .in1(R7Write), .out(multiplexer_5_out), .sel(isWriteEnableR7));
  Multiplexer multiplexer_6 (.in0(JMP), .in1(1'b1), .out(multiplexer_6_out), .sel(isR7));
  RegisterFile8x16 registerfile8x16_1 (
    .A3(A3Out), .Reset(Reset), .WE3(WE3Out), .A1(A1Out), .WD3(WD3Out), .A2(A2Out), .CLK(CLKin),
    .PCCounter(PCPlus1), .RD1(RD1), .RD2(RD2), .RD3(Store), .R7Write(R7Write), .isR7(isR7),
    .isWriteEnable7(isWriteEnableR7));
  ALU alu_1 (.A(AluA), .B(AluB), .ALUOp(OpCode), .Result(ALUResult), .FlagsNZCV(alu_1_flagsnzcv));
  Multiplexer #(.width(16)) multiplexer_7 (.in0(RD2), .in1(ImmOut), .out(AluB), .sel(JMP));
  Multiplexer #(.width(16)) multiplexer_8 (.in0(RD1), .in1(PCOut), .out(AluA), .sel(JMP));
  DataMemory datamemory_1 (
    .DMAddress(ALUResult), .isLoadOrStore(isLoadOrStore), .WE(multiplexer_4_out), .CLK(CLKin),
    .DMDataIn(Store), .DMDataOut(DMData));
  InstructionFetch instructionfetch_1 (
    .WBBus(multiplexer_5_out), .CLK(CLKin), .Reset(Reset), .JMP(multiplexer_6_out), .IMAddress(IMAddress),
    .PCPlus1(PCPlus1));
  flagLatch flaglatch_1 (.ALUFlags(alu_1_flagsnzcv), .CLK(CLKin), .Reset(Reset), .Instruction(IMDataIn), .Flags(Flags));

  assign DMAddress = ALUResult;
  assign IMData = IMDataIn;

  // Other names for the same wires on the sheet: A[15:0] = AluA; B[15:0] = AluB; Result[15:0] = ALUResult
endmodule

module FrontPanelController (
  input  Clk,
  input  Run,
  input  Step,
  input  Reset,
  input  Halt,
  output CpuClk,
  output RunHalt
);

  wire and_1_out, or_1_out, pull_resistor_1_node, t_ff_1_q;

  T_Flip_Flop t_ff_1 (.T(pull_resistor_1_node), .clk(Run), .Q(t_ff_1_q), .reset(Reset));  // open: Qn, preset
  Pull_Resistor #(.pull(1)) pull_resistor_1 (.node(pull_resistor_1_node));
  or or_1 (or_1_out, t_ff_1_q, Step);
  and and_1 (and_1_out, Clk, t_ff_1_q);
  and and_2 (RunHalt, or_1_out, ~Halt);  // AND_Gate
  Multiplexer multiplexer_1 (.in0(Step), .in1(and_1_out), .out(CpuClk), .sel(t_ff_1_q));
endmodule

module InstructionFetch (
  input  [15:0] WBBus,
  input  CLK,
  input  Reset,
  input  JMP,
  output [15:0] IMAddress,
  output [15:0] PCPlus1
);

  wire [15:0] adder_1_out, multiplexer_1_out;

  Adder #(.width(16)) adder_1 (.a({16{1'b0}}), .b(IMAddress), .out(adder_1_out), .cin(1'b1));  // open: cout
  Multiplexer #(.width(16)) multiplexer_1 (.in0(adder_1_out), .in1(WBBus), .out(multiplexer_1_out), .sel(JMP));
  Register #(.width(16)) register_1 (.D(multiplexer_1_out), .en(1'b1), .clk(CLK), .Q(IMAddress), .clr(Reset));
  Adder #(.width(16)) adder_2 (.a(IMAddress), .b({16{1'b0}}), .out(PCPlus1), .cin(1'b1));  // open: cout
endmodule

module ALU (
  input  [15:0] A,
  input  [15:0] B,
  input  [3:0] ALUOp,
  output [15:0] Result,
  output [3:0] FlagsNZCV
);

  wire adder_1_cout, subtractor_1_bout;
  wire [15:0] adder_1_out, alushifter_1_arithshft, alushifter_1_rtteleft, alushifter_1_rtteright,
       alushifter_1_shftleft, alushifter_1_shftright, and_2_out, divider_1_out, divider_1_rem,
       multiplier_1_cout, multiplier_1_out, not_2_out, not_3_out, or_1_out, subtractor_1_out, xor_1_out;

  FlagController flagcontroller_1 (
    .Opcode(ALUOp), .CarryAdd(adder_1_cout), .CarrySub(subtractor_1_bout), .A(A), .B(B), .Result(Result),
    .Carry(FlagsNZCV[1]), .Overflow(FlagsNZCV[0]));
  not not_1 (FlagsNZCV[3], not_2_out[15]);
  assign not_2_out = ~Result;  // NOT_Gate not_2, 16 bits wide
  and and_1 (FlagsNZCV[2], not_2_out[15], not_2_out[14], not_2_out[13], not_2_out[12], not_2_out[11], not_2_out[10], not_2_out[9], not_2_out[8], not_2_out[7], not_2_out[6], not_2_out[5], not_2_out[4], not_2_out[3], not_2_out[2], not_2_out[1], not_2_out[0]);
  Adder #(.width(16)) adder_1 (.a(A), .b(B), .out(adder_1_out), .cout(adder_1_cout));  // open: cin
  Subtractor #(.width(16)) subtractor_1 (.a(A), .b(B), .out(subtractor_1_out), .bout(subtractor_1_bout));  // open: bin
  Multiplier #(.width(16)) multiplier_1 (.a(A), .b(B), .out(multiplier_1_out), .cout(multiplier_1_cout));  // open: cin
  Divider #(.width(16)) divider_1 (.a(A), .b(B), .out(divider_1_out), .rem(divider_1_rem));  // open: upper
  assign and_2_out = A & B;  // AND_Gate and_2, 16 bits wide
  Multiplexer #(.select(4), .width(16)) multiplexer_1 (
    .in0(adder_1_out), .in1(subtractor_1_out), .in2(multiplier_1_out), .in3(multiplier_1_cout),
    .in4(divider_1_out), .in5(divider_1_rem), .in6(and_2_out), .in7(or_1_out), .in8(xor_1_out),
    .in9(not_3_out), .in10(alushifter_1_shftleft), .in11(alushifter_1_shftright),
    .in12(alushifter_1_arithshft), .in13(alushifter_1_rtteleft), .in14(alushifter_1_rtteright),
    .in15({16{1'b0}}), .out(Result), .sel(ALUOp));
  assign or_1_out = A | B;  // OR_Gate or_1, 16 bits wide
  assign xor_1_out = A ^ B;  // XOR_Gate xor_1, 16 bits wide
  assign not_3_out = ~A;  // NOT_Gate not_3, 16 bits wide
  ALUShifter alushifter_1 (
    .SHamt(B[3:0]), .Value(A), .ShftLeft(alushifter_1_shftleft), .ShftRight(alushifter_1_shftright),
    .ArithShft(alushifter_1_arithshft), .RtteLeft(alushifter_1_rtteleft), .RtteRight(alushifter_1_rtteright));
endmodule

module ALUShifter (
  input  [3:0] SHamt,
  input  [15:0] Value,
  output [15:0] ShftLeft,
  output [15:0] ShftRight,
  output [15:0] ArithShft,
  output [15:0] RtteLeft,
  output [15:0] RtteRight
);

  Shifter #(.width(16)) shifter_1 (.in(Value), .\dist (SHamt), .out(ShftLeft));
  Shifter #(.shift("lr"), .width(16)) shifter_2 (.in(Value), .\dist (SHamt), .out(ShftRight));
  Shifter #(.shift("ar"), .width(16)) shifter_3 (.in(Value), .\dist (SHamt), .out(ArithShft));
  Shifter #(.shift("rl"), .width(16)) shifter_4 (.in(Value), .\dist (SHamt), .out(RtteLeft));
  Shifter #(.shift("rr"), .width(16)) shifter_5 (.in(Value), .\dist (SHamt), .out(RtteRight));
endmodule

module FlagController (
  input  [3:0] Opcode,
  input  CarryAdd,
  input  CarrySub,
  input  [15:0] A,
  input  [15:0] B,
  input  [15:0] Result,
  output Carry,
  output Overflow
);

  wire addsubcheck_1_add, addsubcheck_1_sub, and_1_out, and_2_out, and_3_out, and_4_out,
       overflowcheck_1_addoverflow, overflowcheck_1_suboverflow;

  AddSubCheck addsubcheck_1 (.Add(addsubcheck_1_add), .Sub(addsubcheck_1_sub), .OpCode(Opcode));
  OverflowCheck overflowcheck_1 (
    .SubOverflow(overflowcheck_1_suboverflow), .AddOverflow(overflowcheck_1_addoverflow), .A(A), .B(B),
    .Result(Result));
  and and_1 (and_1_out, addsubcheck_1_add, CarryAdd);
  and and_2 (and_2_out, addsubcheck_1_sub, CarrySub);
  and and_3 (and_3_out, addsubcheck_1_add, overflowcheck_1_addoverflow);
  and and_4 (and_4_out, addsubcheck_1_sub, overflowcheck_1_suboverflow);
  or or_1 (Carry, and_1_out, and_2_out);
  or or_2 (Overflow, and_3_out, and_4_out);
endmodule

module AddSubCheck (
  input  [3:0] OpCode,
  output Add,
  output Sub
);

  wire or_1_out;

  or or_1 (or_1_out, OpCode[0], OpCode[1], OpCode[2], OpCode[3]);
  not not_1 (Add, or_1_out);
  and and_1 (Sub, OpCode[0], ~OpCode[1], ~OpCode[2], ~OpCode[3]);  // AND_Gate
endmodule

module OverflowCheck (
  input  [15:0] A,
  input  [15:0] B,
  input  [15:0] Result,
  output AddOverflow,
  output SubOverflow
);

  wire xnor_1_out, xnor_2_out, xor_1_out, xor_2_out;

  xnor xnor_1 (xnor_1_out, A[15], B[15]);
  xor xor_1 (xor_1_out, A[15], Result[15]);
  xor xor_2 (xor_2_out, B[15], A[15]);
  xnor xnor_2 (xnor_2_out, B[15], Result[15]);
  and and_1 (AddOverflow, xnor_1_out, xor_1_out);
  and and_2 (SubOverflow, xor_2_out, xnor_2_out);
endmodule

module RegisterFile8x16 (
  input  [2:0] A3,
  input  Reset,
  input  WE3,
  input  [2:0] A1,
  input  [15:0] WD3,
  input  [2:0] A2,
  input  CLK,
  input  [15:0] PCCounter,
  output [15:0] RD1,
  output [15:0] RD2,
  output [15:0] RD3,
  output [15:0] R7Write,
  output isR7,
  output isWriteEnable7
);

  wire and_2_out, demultiplexer_1_out0, demultiplexer_1_out1, demultiplexer_1_out2, demultiplexer_1_out3,
       demultiplexer_1_out4, demultiplexer_1_out5, demultiplexer_1_out6;
  wire [15:0] demultiplexer_2_out0, demultiplexer_2_out1, demultiplexer_2_out2, demultiplexer_2_out3,
       demultiplexer_2_out4, demultiplexer_2_out5, demultiplexer_2_out6, R0_q, R1_q, R2_q, R3_q, R4_q, R5_q,
       R6_q, WD7;

  Demultiplexer #(.select(3)) demultiplexer_1 (
    .out0(demultiplexer_1_out0), .out1(demultiplexer_1_out1), .out2(demultiplexer_1_out2),
    .out3(demultiplexer_1_out3), .out4(demultiplexer_1_out4), .out5(demultiplexer_1_out5),
    .out6(demultiplexer_1_out6), .out7(isWriteEnable7), .in(WE3), .sel(A3));
  Demultiplexer #(.select(3), .width(16)) demultiplexer_2 (
    .out0(demultiplexer_2_out0), .out1(demultiplexer_2_out1), .out2(demultiplexer_2_out2),
    .out3(demultiplexer_2_out3), .out4(demultiplexer_2_out4), .out5(demultiplexer_2_out5),
    .out6(demultiplexer_2_out6), .out7(WD7), .in(WD3), .sel(A3));
  and and_1 (isR7, A3[0], A3[1], A3[2]);
  Register #(.width(16)) R0 (.D(demultiplexer_2_out0), .en(demultiplexer_1_out0), .clk(CLK), .Q(R0_q), .clr(Reset));
  Register #(.width(16)) R1 (.D(demultiplexer_2_out1), .en(demultiplexer_1_out1), .clk(CLK), .Q(R1_q), .clr(Reset));
  Register #(.width(16)) R2 (.D(demultiplexer_2_out2), .en(demultiplexer_1_out2), .clk(CLK), .Q(R2_q), .clr(Reset));
  Register #(.width(16)) R3 (.D(demultiplexer_2_out3), .en(demultiplexer_1_out3), .clk(CLK), .Q(R3_q), .clr(Reset));
  Register #(.width(16)) R4 (.D(demultiplexer_2_out4), .en(demultiplexer_1_out4), .clk(CLK), .Q(R4_q), .clr(Reset));
  Register #(.width(16)) R5 (.D(demultiplexer_2_out5), .en(demultiplexer_1_out5), .clk(CLK), .Q(R5_q), .clr(Reset));
  Register #(.width(16)) R6 (.D(demultiplexer_2_out6), .en(demultiplexer_1_out6), .clk(CLK), .Q(R6_q), .clr(Reset));
  and and_2 (and_2_out, isWriteEnable7, isR7);
  Multiplexer #(.width(16)) multiplexer_1 (.in0({16{1'b0}}), .in1(WD7), .out(R7Write), .sel(and_2_out));
  Multiplexer #(.select(3), .width(16)) multiplexer_2 (
    .in0(R0_q), .in1(R1_q), .in2(R2_q), .in3(R3_q), .in4(R4_q), .in5(R5_q), .in6(R6_q), .in7(PCCounter),
    .out(RD1), .sel(A1));
  Multiplexer #(.select(3), .width(16)) multiplexer_3 (
    .in0(R0_q), .in1(R1_q), .in2(R2_q), .in3(R3_q), .in4(R4_q), .in5(R5_q), .in6(R6_q), .in7(PCCounter),
    .out(RD2), .sel(A2));
  Multiplexer #(.select(3), .width(16)) multiplexer_4 (
    .in0(R0_q), .in1(R1_q), .in2(R2_q), .in3(R3_q), .in4(R4_q), .in5(R5_q), .in6(R6_q), .in7(PCCounter),
    .out(RD3), .sel(A3));

  // Other names for the same wires on the sheet: WE7 = isWriteEnable7
endmodule

module Controller (
  input  [15:0] Instr,
  input  [15:0] ALUResult,
  input  [15:0] MovData,
  input  [11:0] Imm,
  output [2:0] A3,
  output [2:0] A2,
  output [2:0] A1,
  output [15:0] WD3,
  output WE3,
  output [3:0] OpCode
);

  wire movreg_1_ismov;
  wire [2:0] a3select_1_a3, ainput_1_a1, ainput_1_a3, movreg_1_rd, movreg_1_rn;

  A3Select a3select_1 (
    .Rgstr(Instr[5:3]), .RgstrImm(Instr[14:12]), .ID(Instr[15:13]), .MSB(Instr[15]), .A3(a3select_1_a3));
  WInput winput_1 (
    .Result(ALUResult), .MovData(MovData), .ID(Instr[15:13]), .MSB(Instr[15]), .Instr(Instr), .Imm(Imm),
    .WD3(WD3), .WE3(WE3));
  ALUOp aluop_1 (.OpBits(Instr[12:9]), .ID(Instr[15:13]), .Opcode(OpCode));
  AInput ainput_1 (
    .Addr3(a3select_1_a3), .MSB(Instr[15]), .ID(Instr[15:13]), .Addr2(Instr[2:0]), .Addr1(Instr[8:6]),
    .A3(ainput_1_a3), .A2(A2), .A1(ainput_1_a1));
  movReg movreg_1 (
    .Instruction(Instr), .Rd(movreg_1_rd), .Rn(movreg_1_rn), .isMov(movreg_1_ismov));  // open: flagsOut, isFlag
  Multiplexer #(.width(3)) multiplexer_1 (.in0(ainput_1_a3), .in1(movreg_1_rd), .out(A3), .sel(movreg_1_ismov));
  Multiplexer #(.width(3)) multiplexer_2 (.in0(ainput_1_a1), .in1(movreg_1_rn), .out(A1), .sel(movreg_1_ismov));
endmodule

module signExtend (
  input  [11:0] Imm,
  output [15:0] Extd
);

  wire not_1_out;

  not not_1 (not_1_out, Imm[11]);
  Multiplexer #(.width(4)) multiplexer_1 (.in0(4'b1111), .in1(4'b0000), .out(Extd[15:12]), .sel(not_1_out));

  assign Extd[11:0] = Imm;
endmodule

module AInput (
  input  [2:0] Addr3,
  input  MSB,
  input  [2:0] ID,
  input  [2:0] Addr2,
  input  [2:0] Addr1,
  output [2:0] A3,
  output [2:0] A2,
  output [2:0] A1
);

  wire isaluop_1_bool, or_1_out;

  isALUOp isaluop_1 (.ID(ID), .Bool(isaluop_1_bool));
  or or_1 (or_1_out, MSB, isaluop_1_bool);
  Multiplexer #(.width(3)) multiplexer_1 (.in0(3'b000), .in1(Addr2), .out(A2), .sel(isaluop_1_bool));
  Multiplexer #(.width(3)) multiplexer_2 (.in0(3'b000), .in1(Addr1), .out(A1), .sel(isaluop_1_bool));
  Multiplexer #(.width(3)) multiplexer_3 (.in0(3'b000), .in1(Addr3), .out(A3), .sel(or_1_out));
endmodule

module WInput (
  input  [15:0] Result,
  input  [15:0] MovData,
  input  [2:0] ID,
  input  MSB,
  input  [15:0] Instr,
  input  [11:0] Imm,
  output [15:0] WD3,
  output WE3
);

  wire and_1_out, isaluop_1_bool, ismov_1_ismov, not_1_out, or_1_out, or_2_out;
  wire [15:0] Imm_t, multiplexer_1_out, multiplexer_3_out;

  not not_1 (not_1_out, MSB);
  isALUOp isaluop_1 (.ID(ID), .Bool(isaluop_1_bool));
  isMov ismov_1 (.Instruction(Instr), .isMov(ismov_1_ismov));
  and and_1 (and_1_out, isaluop_1_bool, not_1_out);
  or or_1 (or_1_out, isaluop_1_bool, MSB);
  Multiplexer #(.width(16)) multiplexer_1 (.in0({16{1'b0}}), .in1(Result), .out(multiplexer_1_out), .sel(and_1_out));
  Multiplexer multiplexer_2 (.in0(1'b0), .in1(1'b1), .out(WE3), .sel(or_2_out));
  or or_2 (or_2_out, or_1_out, ismov_1_ismov);
  Multiplexer #(.width(16)) multiplexer_3 (.in0(multiplexer_1_out), .in1(Imm_t), .out(multiplexer_3_out), .sel(MSB));
  Multiplexer #(.width(16)) multiplexer_4 (.in0(multiplexer_3_out), .in1(MovData), .out(WD3), .sel(ismov_1_ismov));
  signExtend signextend_1 (.Imm(Imm), .Extd(Imm_t));
endmodule

module ExtractImm (
  input  [15:0] in_1,
  output [11:0] out_2
);


  assign out_2 = in_1[11:0];
endmodule

module ALUOp (
  input  [3:0] OpBits,
  input  [2:0] ID,
  output [3:0] Opcode
);

  wire isaluop_1_bool;

  isALUOp isaluop_1 (.ID(ID), .Bool(isaluop_1_bool));
  Multiplexer #(.width(4)) multiplexer_1 (.in0(4'b0000), .in1(OpBits), .out(Opcode), .sel(isaluop_1_bool));
endmodule

module A3Select (
  input  [2:0] Rgstr,
  input  [2:0] RgstrImm,
  input  [2:0] ID,
  input  MSB,
  output [2:0] A3
);

  wire and_1_out, isaluop_1_bool, not_1_out;
  wire [2:0] multiplexer_1_out;

  not not_1 (not_1_out, MSB);
  isALUOp isaluop_1 (.ID(ID), .Bool(isaluop_1_bool));
  and and_1 (and_1_out, isaluop_1_bool, not_1_out);
  Multiplexer #(.width(3)) multiplexer_1 (.in0(3'b000), .in1(Rgstr), .out(multiplexer_1_out), .sel(and_1_out));
  Multiplexer #(.width(3)) multiplexer_2 (.in0(multiplexer_1_out), .in1(RgstrImm), .out(A3), .sel(MSB));
endmodule

module isALUOp (
  input  [2:0] ID,
  output Bool
);

  and and_1 (Bool, ID[0], ~ID[1], ~ID[2]);  // AND_Gate
endmodule

module DataMemory (
  input  [15:0] DMAddress,
  input  isLoadOrStore,
  input  WE,
  input  CLK,
  input  [15:0] DMDataIn,
  output [15:0] DMDataOut
);

  wire [15:0] multiplexer_1_out;

  Multiplexer #(.width(16)) multiplexer_1 (
    .in0({16{1'b0}}), .in1(DMAddress), .out(multiplexer_1_out), .sel(isLoadOrStore));
  RAM #(.addrWidth(16), .asyncread("true"), .dataWidth(16)) ram_1 (
    .addr(multiplexer_1_out), .we(WE), .oe(1'b1), .clk(CLK), .din(DMDataIn), .dout(DMDataOut));
endmodule

module flagLatch (
  input  [3:0] ALUFlags,
  input  CLK,
  input  Reset,
  input  [15:0] Instruction,
  output [3:0] Flags
);

  wire WE;

  and and_1 (WE, ~Instruction[15], ~Instruction[14], Instruction[13]);  // AND_Gate
  Register #(.width(4)) register_1 (.D(ALUFlags), .en(WE), .clk(CLK), .Q(Flags), .clr(Reset));
endmodule

module conditionalCircuit (
  input  [15:0] PCPlus1,
  input  [15:0] Instruction,
  input  [3:0] LatchedFlags,
  output [15:0] PCOut,
  output [15:0] ImmOut,
  output JMP,
  output [3:0] Opcode
);

  wire not_1_out;
  wire [11:0] multiplexer_1_out, multiplexer_2_out, multiplexer_3_out;

  Multiplexer #(.width(12)) multiplexer_1 (
    .in0({12{1'b0}}), .in1(Instruction[11:0]), .out(multiplexer_1_out), .sel(LatchedFlags[2]));
  and and_1 (JMP, Instruction[14], ~Instruction[15]);  // AND_Gate
  Multiplexer #(.width(12)) multiplexer_2 (
    .in0({12{1'b0}}), .in1(Instruction[11:0]), .out(multiplexer_2_out), .sel(not_1_out));
  not not_1 (not_1_out, LatchedFlags[2]);
  Multiplexer #(.enable("true"), .select(2), .width(12)) multiplexer_3 (
    .in0(Instruction[11:0]), .in1({12{1'b0}}), .in2(multiplexer_1_out), .in3(multiplexer_2_out),
    .out(multiplexer_3_out), .sel(Instruction[13:12]), .en(JMP));
  signExtend signextend_1 (.Imm(multiplexer_3_out), .Extd(ImmOut));

  assign Opcode = 4'b0000;
  assign PCOut = PCPlus1;

  // Other names for the same wires on the sheet: isZero = LatchedFlags[2]
endmodule

module ZeroExtend (
  input  [3:0] Imm,
  output [15:0] Value
);


  assign Value = {{12{1'b0}}, Imm};
endmodule

module nonALUOps (
  input  [15:0] Instruction,
  input  [3:0] Flags,
  output [15:0] flagsOut,
  output isFlag
);

  wire [3:0] multiplexer_1_out, multiplexer_2_out;

  // AND_Gate and_1 has open pins: in0=Instruction[15], in1=Instruction[14], in2=Instruction[13], in3=Instruction[12], in4=Instruction[11], in5=Instruction[10], in6=Instruction[9], out=open
  and and_2 (isFlag, ~Instruction[15], ~Instruction[14], ~Instruction[13], ~Instruction[12], Instruction[11], ~Instruction[10], Instruction[9]);  // AND_Gate
  Multiplexer #(.width(4)) multiplexer_1 (.in0(4'b0000), .in1(Flags), .out(multiplexer_1_out), .sel(isFlag));
  Multiplexer #(.width(4)) multiplexer_2 (
    .in0(4'b0000), .in1(multiplexer_1_out), .out(multiplexer_2_out), .sel(isFlag));
  ZeroExtend zeroextend_1 (.Imm(multiplexer_2_out), .Value(flagsOut));

  // Other names for the same wires on the sheet: Instr[15:0] = Instruction
endmodule

module movReg (
  input  [15:0] Instruction,
  output [2:0] Rd,
  output [2:0] Rn,
  output [15:0] flagsOut,
  output isFlag,
  output isMov
);

  wire and_1_out, and_3_out, and_4_out, and_5_out, and_6_out, or_1_out;
  wire [2:0] multiplexer_1_out;
  wire [3:0] multiplexer_2_out, multiplexer_5_out;

  and and_1 (and_1_out, ~Instruction[15], ~Instruction[14], ~Instruction[13], ~Instruction[12], Instruction[11], ~Instruction[10], ~Instruction[9]);  // AND_Gate
  and and_2 (isFlag, ~Instruction[15], ~Instruction[14], ~Instruction[13], ~Instruction[12], Instruction[11], ~Instruction[10], Instruction[9]);  // AND_Gate
  and and_3 (and_3_out, Instruction[11], ~Instruction[12], ~Instruction[13], ~Instruction[14], ~Instruction[15]);  // AND_Gate
  Multiplexer #(.width(3)) multiplexer_1 (
    .in0(3'b000), .in1(Instruction[8:6]), .out(multiplexer_1_out), .sel(and_1_out));
  and and_4 (and_4_out, ~Instruction[9], ~Instruction[10]);  // AND_Gate
  and and_5 (and_5_out, Instruction[9], ~Instruction[10]);  // AND_Gate
  Multiplexer #(.width(4)) multiplexer_2 (.in0(4'b0000), .out(multiplexer_2_out), .sel(isFlag));  // open: in1
  and and_6 (and_6_out, and_3_out, or_1_out);
  or or_1 (or_1_out, and_4_out, and_5_out);
  Multiplexer #(.width(3)) multiplexer_3 (.in0(multiplexer_1_out), .in1(3'b000), .out(Rn), .sel(isFlag));
  Multiplexer #(.enable("true"), .select(2), .width(3)) multiplexer_4 (
    .in0(Instruction[5:3]), .in1(Instruction[5:3]), .out(Rd), .sel(Instruction[10:9]), .en(and_6_out));  // open: in2, in3
  Multiplexer #(.width(4)) multiplexer_5 (
    .in0(4'b0000), .in1(multiplexer_2_out), .out(multiplexer_5_out), .sel(isFlag));
  or or_2 (isMov, isFlag, and_1_out);
  ZeroExtend zeroextend_1 (.Imm(multiplexer_5_out), .Value(flagsOut));

  // Other names for the same wires on the sheet: Instr[15:0] = Instruction
endmodule

module isMov (
  input  [15:0] Instruction,
  output isMov
);

  wire and_1_out, and_2_out;

  and and_1 (and_1_out, ~Instruction[15], ~Instruction[14], ~Instruction[13], ~Instruction[12], Instruction[11], ~Instruction[10], ~Instruction[9]);  // AND_Gate
  and and_2 (and_2_out, ~Instruction[15], ~Instruction[14], ~Instruction[13], ~Instruction[12], Instruction[11], ~Instruction[10], Instruction[9]);  // AND_Gate
  or or_1 (isMov, and_1_out, and_2_out);

  // Other names for the same wires on the sheet: Instr[15:0] = Instruction
endmodule

module isNopHalt (
  input  [15:0] Instruction,
  output isNOP,
  output isHalt
);

  wire and_1_out, and_2_out;

  and and_1 (and_1_out, ~Instruction[13], ~Instruction[14], ~Instruction[15]);  // AND_Gate
  and and_2 (and_2_out, ~Instruction[12], ~Instruction[11], ~Instruction[10], ~Instruction[9]);  // AND_Gate
  and and_3 (isHalt, ~Instruction[12], ~Instruction[11], Instruction[10], Instruction[9]);  // AND_Gate
  and and_4 (isNOP, and_2_out, and_1_out);

  // Other names for the same wires on the sheet: Instr[15:0] = Instruction
endmodule

module LoadStore (
  input  [15:0] Instruction,
  output [2:0] Rd,
  output [2:0] Rm,
  output [2:0] Rn,
  output isLoad,
  output isLoadOrStore,
  output isStore
);

  wire not_1_out, or_1_out;

  and and_1 (isLoad, ~Instruction[9], ~Instruction[10], ~Instruction[11], Instruction[12], ~Instruction[13], ~Instruction[14], ~Instruction[15]);  // AND_Gate
  and and_2 (isStore, ~Instruction[9], ~Instruction[10], Instruction[11], Instruction[12], ~Instruction[13], ~Instruction[14], ~Instruction[15]);  // AND_Gate
  or or_1 (or_1_out, isLoad, isStore);
  Multiplexer #(.width(3)) multiplexer_1 (.in0(Instruction[5:3]), .in1(3'b000), .out(Rd), .sel(not_1_out));
  Multiplexer #(.width(3)) multiplexer_2 (.in0(Instruction[2:0]), .in1(3'b000), .out(Rm), .sel(not_1_out));
  Multiplexer #(.width(3)) multiplexer_3 (.in0(Instruction[8:6]), .in1(3'b000), .out(Rn), .sel(not_1_out));
  not not_1 (not_1_out, or_1_out);
  or or_2 (isLoadOrStore, isLoad, isStore);

  // Other names for the same wires on the sheet: Instr[15:0] = Instruction
endmodule

module RegisterFileControl (
  input  isLoadOrStore,
  input  WE3,
  input  [2:0] A1,
  input  [2:0] LoadStoreRm,
  input  [2:0] A2,
  input  [2:0] LoadStoreRn,
  input  [2:0] A3,
  input  [2:0] LoadStoreRd,
  input  [15:0] WD3,
  input  [15:0] DMData,
  input  isLoad,
  input  in_12,
  output WE3Out,
  output [2:0] A1Out,
  output [2:0] A2Out,
  output [2:0] A3Out,
  output [15:0] WD3Out
);

  Multiplexer #(.width(3)) multiplexer_1 (.in0(A3), .in1(LoadStoreRd), .out(A3Out), .sel(isLoadOrStore));
  Multiplexer multiplexer_2 (.in0(WE3), .in1(1'b1), .out(WE3Out), .sel(isLoad));
  Multiplexer #(.width(3)) multiplexer_3 (.in0(A1), .in1(LoadStoreRm), .out(A1Out), .sel(isLoadOrStore));
  Multiplexer #(.width(3)) multiplexer_4 (.in0(A2), .in1(LoadStoreRn), .out(A2Out), .sel(isLoadOrStore));
  Multiplexer #(.width(16)) multiplexer_5 (.in0(WD3), .in1(DMData), .out(WD3Out), .sel(isLoad));

  // Other names for the same wires on the sheet: isFlags = in_12
endmodule
